// Logisim project Atividade ULA - Circuito da Calculadora.circ as structural Verilog: 1 circuit, main circuit main
module main (
  input  C,
  input  D,
  input  B,
  input  A
);

  wire A___0_2_out, A___0_3_out, A___0_4_out, A___0_5_out, A___0_6_out, A___0_7_out, A___0_8_out,
       A___0_9_out, A___0_10_out, A___0_11_out, A___0_12_out, A___0_13_out, A___0_14_out, A___0_15_out,
       A___0_16_out, A___0_17_out, A___0_18_out, A___0_19_out, A___0_20_out, A___0_21_out, A___0_22_out,
       A___0_out, A___1_2_out, A___1_3_out, A___1_4_out, A___1_5_out, A___1_6_out, A___1_7_out, A___1_8_out,
       A___1_9_out, A___1_10_out, A___1_11_out, A___1_12_out, A___1_13_out, A___1_14_out, A___1_15_out,
       A___1_16_out, A___1_17_out, A___1_18_out, A___1_19_out, A___1_20_out, A___1_21_out, A___1_out,
       and_1_out, and_2_out, and_3_out, and_4_out, B___0_2_out, B___0_3_out, B___0_4_out, B___0_5_out,
       B___0_6_out, B___0_7_out, B___0_8_out, B___0_9_out, B___0_10_out, B___0_11_out, B___0_12_out,
       B___0_13_out, B___0_14_out, B___0_15_out, B___0_16_out, B___0_17_out, B___0_18_out, B___0_19_out,
       B___0_20_out, B___0_21_out, B___0_22_out, B___0_23_out, B___0_24_out, B___0_25_out, B___0_26_out,
       B___0_27_out, B___0_28_out, B___0_29_out, B___0_30_out, B___0_31_out, B___0_32_out, B___0_33_out,
       B___0_34_out, B___0_35_out, B___0_36_out, B___0_37_out, B___0_38_out, B___0_39_out, B___0_40_out,
       B___0_41_out, B___0_42_out, B___0_out, B___1_2_out, B___1_3_out, B___1_4_out, B___1_5_out,
       B___1_6_out, B___1_7_out, B___1_8_out, B___1_9_out, B___1_10_out, B___1_11_out, B___1_12_out,
       B___1_13_out, B___1_14_out, B___1_15_out, B___1_16_out, B___1_17_out, B___1_18_out, B___1_19_out,
       B___1_20_out, B___1_21_out, B___1_22_out, B___1_23_out, B___1_24_out, B___1_25_out, B___1_26_out,
       B___1_27_out, B___1_28_out, B___1_29_out, B___1_30_out, B___1_31_out, B___1_32_out, B___1_33_out,
       B___1_34_out, B___1_35_out, B___1_36_out, B___1_37_out, B___1_38_out, B___1_39_out, B___1_40_out,
       B___1_41_out, B___1_42_out, B___1_out, F_out, G_out, H_out, I_out, J_out, K_out, L_out, M_out, N_out,
       nand_1_out, nor_1_out, not_1_out, not_2_out, not_3_out, not_4_out, not_5_out, O_out, or_1_out,
       or_2_out, or_3_out, or_4_out, or_5_out, or_6_out, or_7_out, or_8_out, or_9_out, or_10_out, or_11_out,
       or_12_out, or_13_out, or_14_out, or_15_out, or_16_out, or_17_out, or_18_out, or_19_out, or_20_out,
       or_21_out, or_22_out, or_23_out, or_24_out, or_25_out, or_26_out, or_27_out, or_28_out, or_29_out,
       or_30_out, or_31_out, or_32_out, or_33_out, or_34_out, or_35_out, or_36_out, or_37_out, or_38_out,
       or_39_out, or_40_out, or_41_out, or_42_out, or_43_out, or_44_out, or_45_out, or_46_out, or_47_out,
       or_48_out, or_49_out, or_50_out, or_51_out, or_52_out, or_53_out, or_54_out, or_55_out, P_out, Q_out,
       R_out, S_out, T_out, U_out, V_out, W_out, X_out, xor_1_out, Y_out;

  not not_1 (not_1_out, C);
  not not_2 (not_2_out, D);
  or or_1 (or_1_out, D, not_2_out);
  and and_1 (and_1_out, D, not_2_out);
  or or_2 (or_2_out, C, not_2_out);
  or or_3 (or_3_out, C, not_2_out);
  and and_2 (and_2_out, not_1_out, not_2_out);
  or or_4 (or_4_out, not_1_out, D);
  or or_5 (or_5_out, C, not_2_out);
  xor xor_1 (xor_1_out, C, D);
  or or_6 (or_6_out, not_1_out, D);
  or or_7 (or_7_out, D, C);
  or or_8 (or_8_out, not_2_out, D);
  nor nor_1 (nor_1_out, D, C);
  and and_3 (and_3_out, C, D);
  or or_9 (or_9_out, D, C);
  and and_4 (and_4_out, not_1_out, D);
  or or_10 (or_10_out, not_2_out, D);
  or or_11 (or_11_out, D, not_2_out);
  nand nand_1 (nand_1_out, D, C);
  not not_3 (not_3_out, C);
  or or_12 (or_12_out, not_1_out, D);
  not not_4 (not_4_out, nor_1_out);
  not not_5 (not_5_out, B);
  and B___0 (B___0_out, not_5_out, or_1_out);
  and B___1 (B___1_out, B, and_1_out);
  and B___0_2 (B___0_2_out, not_5_out, and_1_out);
  and B___1_2 (B___1_2_out, B, and_1_out);
  and B___1_3 (B___1_3_out, B, or_1_out);
  and B___0_3 (B___0_3_out, not_5_out, or_1_out);
  and B___1_4 (B___1_4_out, B, or_1_out);
  and B___0_4 (B___0_4_out, not_5_out, or_3_out);
  and B___1_5 (B___1_5_out, B, or_3_out);
  and B___0_5 (B___0_5_out, not_5_out, and_2_out);
  and B___1_6 (B___1_6_out, B, and_2_out);
  and B___1_7 (B___1_7_out, B, or_1_out);
  and B___1_8 (B___1_8_out, B, or_1_out);
  and B___0_6 (B___0_6_out, not_5_out, or_5_out);
  and B___1_9 (B___1_9_out, B, xor_1_out);
  and B___0_7 (B___0_7_out, not_5_out, C);
  and B___1_10 (B___1_10_out, B, or_9_out);
  and B___0_8 (B___0_8_out, not_5_out, nor_1_out);
  and B___1_11 (B___1_11_out, B, and_3_out);
  and B___0_9 (B___0_9_out, not_5_out, or_10_out);
  and B___1_12 (B___1_12_out, B, or_11_out);
  and B___0_10 (B___0_10_out, not_5_out, or_1_out);
  and B___1_13 (B___1_13_out, B, and_1_out);
  and B___0_11 (B___0_11_out, not_5_out, or_1_out);
  and B___1_14 (B___1_14_out, B, or_1_out);
  and B___0_12 (B___0_12_out, not_5_out, and_1_out);
  and B___1_15 (B___1_15_out, B, and_1_out);
  and B___0_13 (B___0_13_out, not_5_out, or_1_out);
  and B___1_16 (B___1_16_out, B, or_1_out);
  and B___0_14 (B___0_14_out, not_5_out, or_1_out);
  and B___1_17 (B___1_17_out, B, or_1_out);
  and B___0_15 (B___0_15_out, not_5_out, or_1_out);
  and B___1_18 (B___1_18_out, B, and_1_out);
  and B___0_16 (B___0_16_out, not_5_out, or_1_out);
  and B___1_19 (B___1_19_out, B, and_1_out);
  and B___0_17 (B___0_17_out, not_5_out, or_1_out);
  and B___0_18 (B___0_18_out, not_5_out, or_1_out);
  and B___0_19 (B___0_19_out, not_5_out, or_1_out);
  and B___1_20 (B___1_20_out, B, or_1_out);
  and B___0_20 (B___0_20_out, not_5_out, and_1_out);
  and B___1_21 (B___1_21_out, B, or_1_out);
  and B___0_21 (B___0_21_out, not_5_out, or_2_out);
  and B___1_22 (B___1_22_out, B, or_2_out);
  and B___0_22 (B___0_22_out, not_5_out, or_2_out);
  and B___1_23 (B___1_23_out, B, or_2_out);
  and B___0_23 (B___0_23_out, not_5_out, C);
  and B___0_24 (B___0_24_out, not_5_out, C);
  and B___0_25 (B___0_25_out, not_5_out, or_3_out);
  and B___1_24 (B___1_24_out, B, or_3_out);
  and B___0_26 (B___0_26_out, not_5_out, and_2_out);
  and B___1_25 (B___1_25_out, B, and_2_out);
  and B___0_27 (B___0_27_out, not_5_out, not_2_out);
  and B___1_26 (B___1_26_out, B, not_2_out);
  and B___0_28 (B___0_28_out, not_5_out, not_2_out);
  and B___0_29 (B___0_29_out, not_5_out, or_1_out);
  and B___0_30 (B___0_30_out, not_5_out, or_1_out);
  and B___0_31 (B___0_31_out, not_5_out, or_4_out);
  and B___1_27 (B___1_27_out, B, or_4_out);
  and B___0_32 (B___0_32_out, not_5_out, or_5_out);
  and B___1_28 (B___1_28_out, B, xor_1_out);
  and B___0_33 (B___0_33_out, not_5_out, or_6_out);
  and B___1_29 (B___1_29_out, B, or_5_out);
  and B___0_34 (B___0_34_out, not_5_out, C);
  and B___0_35 (B___0_35_out, not_5_out, or_8_out);
  and B___0_36 (B___0_36_out, not_5_out, or_6_out);
  and B___1_30 (B___1_30_out, B, or_5_out);
  and B___0_37 (B___0_37_out, not_5_out, nor_1_out);
  and B___1_31 (B___1_31_out, B, and_3_out);
  and B___0_38 (B___0_38_out, not_5_out, not_2_out);
  and B___1_32 (B___1_32_out, B, and_4_out);
  and B___0_39 (B___0_39_out, not_5_out, nand_1_out);
  and B___1_33 (B___1_33_out, B, not_3_out);
  and B___0_40 (B___0_40_out, not_5_out, or_12_out);
  and B___1_34 (B___1_34_out, B, or_5_out);
  or or_13 (or_13_out, B___0_out, B___1_out);
  or or_14 (or_14_out, B___0_14_out, B___1_17_out);
  or or_15 (or_15_out, B___0_15_out, B___1_18_out);
  or or_16 (or_16_out, B___0_2_out, B___1_2_out);
  and B___1_35 (B___1_35_out, B, and_1_out);
  and B___1_36 (B___1_36_out, B, C);
  and B___1_37 (B___1_37_out, B, C);
  or or_17 (or_17_out, B___0_4_out, B___1_5_out);
  or or_18 (or_18_out, B___0_25_out, B___1_24_out);
  or or_19 (or_19_out, B___0_26_out, B___1_25_out);
  or or_20 (or_20_out, B___0_5_out, B___1_6_out);
  and B___1_38 (B___1_38_out, B, not_2_out);
  and B___0_41 (B___0_41_out, not_5_out, or_4_out);
  and B___1_39 (B___1_39_out, B, or_4_out);
  and B___1_40 (B___1_40_out, B, or_7_out);
  and B___1_41 (B___1_41_out, B, or_8_out);
  or or_21 (or_21_out, B___0_6_out, B___1_9_out);
  or or_22 (or_22_out, B___0_36_out, B___1_30_out);
  or or_23 (or_23_out, B___0_37_out, B___1_31_out);
  or or_24 (or_24_out, B___0_7_out, B___1_10_out);
  and B___0_42 (B___0_42_out, not_5_out, not_4_out);
  and B___1_42 (B___1_42_out, B, or_10_out);
  or or_25 (or_25_out, B___0_10_out, B___1_13_out);
  or or_26 (or_26_out, B___0_11_out, B___1_14_out);
  or or_27 (or_27_out, B___0_12_out, B___1_15_out);
  or or_28 (or_28_out, B___0_13_out, B___1_16_out);
  or or_29 (or_29_out, B___0_16_out, B___1_19_out);
  or or_30 (or_30_out, B___0_17_out, B___1_35_out);
  or or_31 (or_31_out, B___0_18_out, B___1_3_out);
  or or_32 (or_32_out, B___0_3_out, B___1_4_out);
  or or_33 (or_33_out, B___0_19_out, B___1_20_out);
  or or_34 (or_34_out, B___0_20_out, B___1_21_out);
  or or_35 (or_35_out, B___0_21_out, B___1_22_out);
  or or_36 (or_36_out, B___0_23_out, B___1_36_out);
  or or_37 (or_37_out, B___0_24_out, B___1_37_out);
  or or_38 (or_38_out, B___0_27_out, B___1_26_out);
  or or_39 (or_39_out, B___0_28_out, B___1_38_out);
  or or_40 (or_40_out, B___0_29_out, B___1_7_out);
  or or_41 (or_41_out, B___0_30_out, B___1_8_out);
  or or_42 (or_42_out, B___0_31_out, B___1_27_out);
  or or_43 (or_43_out, B___0_41_out, B___1_39_out);
  or or_44 (or_44_out, B___0_32_out, B___1_28_out);
  or or_45 (or_45_out, B___0_34_out, B___1_40_out);
  or or_46 (or_46_out, B___0_35_out, B___1_41_out);
  or or_47 (or_47_out, B___0_38_out, B___1_32_out);
  or or_48 (or_48_out, B___0_8_out, B___1_11_out);
  or or_49 (or_49_out, B___0_9_out, B___1_12_out);
  or or_50 (or_50_out, B___0_39_out, B___1_33_out);
  or or_51 (or_51_out, B___0_40_out, B___1_34_out);
  or or_52 (or_52_out, B___0_42_out, B___1_42_out);
  or or_53 (or_53_out, B___0_22_out, B___1_23_out);
  or or_54 (or_54_out, B___0_33_out, B___1_29_out);
  not A___0 (A___0_out, A);
  and A___1 (A___1_out, A, or_28_out);
  and A___0_2 (A___0_2_out, A___0_out, or_13_out);
  and A___1_2 (A___1_2_out, A, or_14_out);
  and A___0_3 (A___0_3_out, A___0_out, or_15_out);
  and A___1_3 (A___1_3_out, A, or_16_out);
  and A___0_4 (A___0_4_out, A___0_out, or_19_out);
  and A___1_4 (A___1_4_out, A, or_20_out);
  and A___0_5 (A___0_5_out, A___0_out, or_23_out);
  and A___1_5 (A___1_5_out, A, or_24_out);
  or G (G_out, A___0_2_out, A___1_2_out);
  and A___1_6 (A___1_6_out, A, or_30_out);
  and A___0_6 (A___0_6_out, A___0_out, or_33_out);
  and A___1_7 (A___1_7_out, A, or_34_out);
  and A___1_8 (A___1_8_out, A, or_37_out);
  and A___0_7 (A___0_7_out, A___0_out, or_17_out);
  and A___1_9 (A___1_9_out, A, or_18_out);
  and A___1_10 (A___1_10_out, A, or_39_out);
  and A___0_8 (A___0_8_out, A___0_out, or_42_out);
  and A___1_11 (A___1_11_out, A, or_43_out);
  and A___1_12 (A___1_12_out, A, or_46_out);
  and A___0_9 (A___0_9_out, A___0_out, or_21_out);
  and A___1_13 (A___1_13_out, A, or_22_out);
  and A___1_14 (A___1_14_out, A, or_48_out);
  and A___0_10 (A___0_10_out, A___0_out, or_51_out);
  and A___1_15 (A___1_15_out, A, or_52_out);
  and A___0_11 (A___0_11_out, A___0_out, or_25_out);
  and A___1_16 (A___1_16_out, A, or_26_out);
  and A___0_12 (A___0_12_out, A___0_out, or_29_out);
  and A___0_13 (A___0_13_out, A___0_out, or_31_out);
  and A___1_17 (A___1_17_out, A, or_32_out);
  and A___0_14 (A___0_14_out, A___0_out, or_35_out);
  and A___1_18 (A___1_18_out, A, or_53_out);
  or N (N_out, A___0_7_out, A___1_9_out);
  and A___0_15 (A___0_15_out, A___0_out, or_38_out);
  and A___0_16 (A___0_16_out, A___0_out, or_40_out);
  and A___1_19 (A___1_19_out, A, or_41_out);
  and A___0_17 (A___0_17_out, A___0_out, or_44_out);
  and A___1_20 (A___1_20_out, A, or_54_out);
  or U (U_out, A___0_9_out, A___1_13_out);
  and A___0_18 (A___0_18_out, A___0_out, or_47_out);
  and A___0_19 (A___0_19_out, A___0_out, or_49_out);
  and A___1_21 (A___1_21_out, A, or_50_out);
  and A___0_20 (A___0_20_out, A___0_out, or_27_out);
  or H (H_out, A___0_3_out, A___1_3_out);
  or I (I_out, A___0_12_out, A___1_6_out);
  and A___0_21 (A___0_21_out, A___0_out, or_36_out);
  or O (O_out, A___0_4_out, A___1_4_out);
  or P (P_out, A___0_15_out, A___1_10_out);
  and A___0_22 (A___0_22_out, A___0_out, or_45_out);
  or V (V_out, A___0_5_out, A___1_5_out);
  or W (W_out, A___0_18_out, A___1_14_out);
  or or_55 (or_55_out, A___0_11_out, A___1_16_out);
  or K (K_out, A___0_6_out, A___1_7_out);
  or L (L_out, A___0_14_out, A___1_18_out);
  or R (R_out, A___0_8_out, A___1_11_out);
  or S (S_out, A___0_17_out, A___1_20_out);
  or Y (Y_out, A___0_10_out, A___1_15_out);
  or F (F_out, A___0_20_out, A___1_out);
  or J (J_out, A___0_13_out, A___1_17_out);
  or M (M_out, A___0_21_out, A___1_8_out);
  or Q (Q_out, A___0_16_out, A___1_19_out);
  or T (T_out, A___0_22_out, A___1_12_out);
  or X (X_out, A___0_19_out, A___1_21_out);
  _7_Segment_Display u_7_segment_display_1 (
    .g(F_out), .f(H_out), .a(or_55_out), .b(J_out), .e(I_out), .d(G_out), .c(K_out));  // open: dp
  _7_Segment_Display u_7_segment_display_2 (
    .g(M_out), .f(O_out), .a(L_out), .b(Q_out), .e(P_out), .d(N_out), .c(R_out));  // open: dp
  _7_Segment_Display u_7_segment_display_3 (
    .g(T_out), .f(V_out), .a(S_out), .b(X_out), .e(W_out), .d(U_out), .c(Y_out));  // open: dp

  // Notes on the sheet:
  //   A = 1
  //   A = 1
  //   A = 1
  //   E
  //   +
  //   =
endmodule
